# Fritzing sketch SimpleBreadboardButtonLed (saved by Fritzing 0.9.0b)
breadboards: 1

parts:
  Netduino_Plus_1 = Netduino Plus 2
  R1 = Resistor [tolerance=±5% resistance=330 package=THT]
  LED1 = LED - 5mm [color="Red (633nm)" package="5 mm [THT]"]
  S1 = Pushbutton [package="[THT]"]

nets:
  N1: Netduino_Plus_1.GND, LED1.cathode, S1.Pin_3, S1.Pin_4
  N2: Netduino_Plus_1.D1, S1.Pin_1, S1.Pin_2
  N3: Netduino_Plus_1.D0, R1.Pin_1
  N4: R1.Pin_0, LED1.anode

custom parts:
  Netduino Plus 2: An open-source electronics platform using the .NET Micro Framework
