# Fritzing sketch SimplePiezoSpeaker (saved by Fritzing 0.9.0b)
breadboards: 1

parts:
  Netduino_Plus_1 = Netduino Plus 2
  J1 = Piezo Speaker

nets:
  N1: Netduino_Plus_1.GND, J1.pin1
  N2: Netduino_Plus_1.D5, J1.pin2

custom parts:
  Netduino Plus 2: An open-source electronics platform using the .NET Micro Framework
