# Fritzing sketch SimpleRgbLed (saved by Fritzing 0.9.0b)
breadboards: 1

parts:
  Netduino_Plus_1 = Netduino Plus 2
  R1 = Resistor [tolerance=±5% resistance=330 package=THT]
  R2 = Resistor [tolerance=±5% resistance=330 package=THT]
  R3 = Resistor [tolerance=±5% resistance=330 package=THT]
  LED1 = RGB LED (com. cathode, rgb) [package="5 mm [THT]"]
  LED2 = RGB LED (com. cathode, rgb) [package="5 mm [THT]"]
  R4 = Resistor [tolerance=±5% resistance=330 package=THT]
  R5 = Resistor [tolerance=±5% resistance=330 package=THT]
  R6 = Resistor [tolerance=±5% resistance=330 package=THT]

nets:
  N1: Netduino_Plus_1.GND, LED1.common_cathode, LED2.common_cathode
  N2: Netduino_Plus_1.D11, R4.Pin_1
  N3: Netduino_Plus_1.D9, R5.Pin_1
  N4: Netduino_Plus_1.D8, R6.Pin_1
  N5: Netduino_Plus_1.D7, R1.Pin_1
  N6: Netduino_Plus_1.D5, R2.Pin_1
  N7: Netduino_Plus_1.D4, R3.Pin_1
  N8: R1.Pin_0, LED1.red_anode
  N9: R2.Pin_0, LED1.green_anode
  N10: R3.Pin_0, LED1.blue_anode
  N11: LED2.red_anode, R4.Pin_0
  N12: LED2.green_anode, R5.Pin_0
  N13: LED2.blue_anode, R6.Pin_0

custom parts:
  Netduino Plus 2: An open-source electronics platform using the .NET Micro Framework
